# Fritzing sketch Termometer-ds18b20 (saved by Fritzing 0.9.3b)
breadboards: 1

parts:
  DS1 = DS18B20 1-Wire Temperature Sensor [part_number=DS18B20]
  Part1 = Arduino Uno (Rev3)
  R1 = Resistor [tolerance=±5% resistance=4.7k package=THT]

nets:
  GND: DS1.GND, Part1.GND
  N1: DS1.DQ, Part1.D2, R1.Pin_0
  VDD: DS1.VDD, Part1.3V3, R1.Pin_1
