# Fritzing sketch Termometer-with-LCD (saved by Fritzing 0.9.3b)
breadboards: 1

parts:
  Part2 = Arduino Uno (Rev3)
  DHT2 = DHT11 Humitidy and Temperature Sensor
  R2 = Resistor [tolerance=±5% resistance=10k package=THT]
  Part3 = LCD1602-I2C

nets:
  N1: Part2.A4/SDA, Part3.SDA
  N2: Part2.A5/SCL, Part3.SCL
  N3: Part2.D2, DHT2.DATA, R2.Pin_0
  5V: Part2.5V, DHT2.VDD, R2.Pin_1, Part3.VCC
  GND: Part2.GND, DHT2.GND, Part3.GND

custom parts:
  DHT11 Humitidy and Temperature Sensor: DHT11 Humidity and Temperature Sensor
  LCD1602-I2C: A standard character display, usually with 2x16 characters. Comes in many colors with LCM1602 IIC attached.
