# Fritzing sketch Termometer (saved by Fritzing 0.9.3b)
circuit board: 8.46667cm x 5.64444cm
breadboards: 1

parts:
  Part1 = Arduino Uno (Rev3)
  DHT1 = DHT11 Humitidy and Temperature Sensor
  R1 = Resistor [tolerance=±5% resistance=10k package=THT]
  Grove1 = Grove 4 Digit Display

nets (from the breadboard view):
  N1: Part1.D2, DHT1.DATA, R1.Pin_0
  N2: Part1.D3_PWM, Grove1.CLK
  N3: Part1.D4, Grove1.DIO
  5V: Part1.5V, DHT1.VDD, R1.Pin_1, Grove1.VCC
  GND: Part1.GND, DHT1.GND, Grove1.GND

custom parts:
  DHT11 Humitidy and Temperature Sensor: DHT11 Humidity and Temperature Sensor
