# Fritzing sketch relay (saved by Fritzing 0.9.3b)

parts:
  Part3 = Arduino Uno (Rev3)
  KY-3 = Keyes Relay [package=THT]
  VCC1 = Battery block 9V
  LED2 = Billie the Blue LED
  R1 = Resistor [tolerance=±5% resistance=220 package="0805 [SMD]"]
  VCC2 = 4 x AAA Battery Mount

nets:
  N1: Part3.D4, KY-3.signal
  N2: Part3.GND, KY-3.ground, VCC2.-
  N3: KY-3.power, VCC2.+
  N4: KY-3.NC, VCC1.+
  N5: KY-3.C, R1.Pin_0
  N6: LED2.anode, R1.Pin_1

custom parts:
  Keyes Relay: The Keyes 5V relay module is suitable for SCM development, home appliance control. It uses a 5V~12V TIL control signal which can control DC / AC signal.
