# Fritzing sketch moter-sketch (saved by Fritzing 0.9.3b)
breadboards: 1

parts:
  part = Arduino Uno (Rev3) - ICSP
  part_2 = Pushbutton [package="[THT]"]
  part_3 = Rectifier Diode [part_number=1N4007 package="300 mil [THT]"]
  BAT1 = BC9VPC [package=bc9vpc]
  part_4 = DC Motor
  R1 = Resistor [tolerance=±5% resistance=10k package=THT]
  part_5 = Basic FET N-Channel [package="TO220 [THT]"]

nets:
  N1: part.5V, part_2.Pin_1, part_2.Pin_2
  N2: part.GND, BAT1.V-, R1.Pin_0, part_5.source
  N3: part.D9_PWM, part_5.gate
  N4: part.D2, part_2.Pin_3, part_2.Pin_4, R1.Pin_1
  N5: part_3.cathode, BAT1.V+, part_4.pin_2
  N6: part_3.anode, part_4.pin_1, part_5.drain
