# Fritzing sketch servo-sketch (saved by Fritzing 0.9.3b)
breadboards: 1

parts:
  part = Arduino Uno (Rev3)
  part_2 = Basic Servo
  C1 = Electrolytic Capacitor [capacitance=100µF voltage=10V package="200 mil [THT, electrolytic]"]
  C2 = Electrolytic Capacitor [capacitance=100µF voltage=10V package="200 mil [THT, electrolytic]"]
  R1 = Rotary Potentiometer (Small) [maximum_resistance=100kΩ package=THT]

nets:
  N1: part.A0, R1.wiper
  N2: part.D9_PWM, part_2.pulse
  5V: part.5V, part_2.vcc, C1.+, C2.+, R1.leg2
  GND: part.GND, part_2.gnd, C1.-, C2.-, R1.leg1
