# Fritzing sketch gyro (saved by Fritzing 0.9.3b)

parts:
  Part1 = Arduino Uno (Rev3)
  GY2 = MPU-6050 Board GY-521 [form="♀ (female)" package=THT]

nets:
  N1: Part1.A4/SDA, GY2.pin4
  N2: Part1.A5/SCL, GY2.pin3
  N3: Part1.D2, GY2.pin8
  N4: Part1.5V, GY2.pin1
  N5: Part1.GND, GY2.pin2, GY2.pin7

custom parts:
  MPU-6050 Board GY-521: Acelerometro y Giroscopio MPU-6050 Board GY-521
