# Fritzing sketch micro-sd (saved by Fritzing 0.9.3b)

parts:
  Part1 = MicroSD Card Module
  Part2 = Arduino Uno (Rev3)

nets:
  GND: Part1.GND, Part2.GND
  VCC: Part1.VCC, Part2.5V
  N1: Part1.MISO, Part2.D12/MISO
  N2: Part1.MOSI, Part2.D11_PWM/MOSI
  N3: Part1.SCK, Part2.D13/SCK
  N4: Part1.CS, Part2.D4
